// Logisim project proj.circ as structural Verilog: 1 circuit, main circuit main
module main (
);

  wire clk, debugger_1_p1, mem, not_1_out, r_w, read, word;
  wire [6:0] keyboard_1_data;
  wire [15:0] addr, data, debugger_1_p4, debugger_1_p5, fp, pc, ps, r0, r1, r2, r3, r4, r5, r6, sp;

  // Probe on r0
  // Probe on fp
  Clock clock_1 (.out(clk));
  // Probe on r2
  // Probe on r1
  // Probe on sp
  // Probe on pc
  // CdM_16 cdm_16_1: pin names not known; wires that end beside it: r0, r1, r2, r3, r4, r5, r6, fp, pc, sp, ps, mem, r_w, word, addr
  // Debugger debugger_1: pin names not known; wires that end beside it: debugger_1_p1, 1'b0, clk, debugger_1_p4, debugger_1_p5
  // Probe on r4
  // Probe on r3
  // Probe on ps
  // Probe on r5
  // Probe on r6
  assign data = not_1_out ? debugger_1_p4 : 16'bz;  // Controlled_Buffer controlled_buffer_1
  not not_1 (not_1_out, r_w);
  assign debugger_1_p5 = r_w ? data : 16'bz;  // Controlled_Buffer controlled_buffer_2
  Keyboard keyboard_1 (.clk(clk), .data(keyboard_1_data));  // open: re, clr, avail
  TTY tty_1 (.data(keyboard_1_data), .clk(clk));  // open: we, clr
  // RAM ram_1: pin names not known; wires that end beside it: debugger_1_p1, addr, word, mem, clk, read, data
  // ROM rom_1: pin names not known; wires that end beside it: debugger_1_p1

  // Notes on the sheet:
  //   Процессор
  //   Память
  //   Терминал
endmodule
